# Fritzing sketch pcb (saved by Fritzing 0.8.0b)
breadboards: 1

parts:
  S1 = Reed switch [package=THT]  # not connected
  S2 = Reed switch [package=THT]  # not connected
  S3 = Reed switch [package=THT]  # not connected
  S4 = Reed switch [package=THT]  # not connected
  S5 = Reed switch [package=THT]  # not connected
  S6 = Reed switch [package=THT]  # not connected
  S7 = Reed switch [package=THT]  # not connected
  S8 = Reed switch [package=THT]  # not connected
  S9 = Reed switch [package=THT]  # not connected
  S10 = Reed switch [package=THT]  # not connected
  S12 = Reed switch [package=THT]  # not connected
  S13 = Reed switch [package=THT]  # not connected
  S14 = Reed switch [package=THT]  # not connected
  S15 = Reed switch [package=THT]  # not connected
  S16 = Reed switch [package=THT]  # not connected
  S17 = Reed switch [package=THT]  # not connected
  S18 = Reed switch [package=THT]  # not connected
  S19 = Reed switch [package=THT]  # not connected
  S20 = Reed switch [package=THT]
  S21 = Reed switch [package=THT]
  S22 = Reed switch [package=THT]
  S23 = Reed switch [package=THT]
  S24 = Reed switch [package=THT]
  S25 = Reed switch [package=THT]
  S26 = Reed switch [package=THT]
  S27 = Reed switch [package=THT]
  S28 = Reed switch [package=THT]
  S29 = Reed switch [package=THT]  # not connected
  S30 = Reed switch [package=THT]  # not connected
  S31 = Reed switch [package=THT]  # not connected
  S32 = Reed switch [package=THT]  # not connected
  S33 = Reed switch [package=THT]  # not connected
  S34 = Reed switch [package=THT]  # not connected
  S35 = Reed switch [package=THT]  # not connected
  S36 = Reed switch [package=THT]  # not connected
  S37 = Reed switch [package=THT]  # not connected
  S38 = Reed switch [package=THT]  # not connected
  S39 = Reed switch [package=THT]  # not connected
  S40 = Reed switch [package=THT]  # not connected
  S41 = Reed switch [package=THT]  # not connected
  S42 = Reed switch [package=THT]  # not connected
  S43 = Reed switch [package=THT]  # not connected
  S44 = Reed switch [package=THT]  # not connected
  S45 = Reed switch [package=THT]  # not connected
  S46 = Reed switch [package=THT]  # not connected
  S48 = Reed switch [package=THT]  # not connected
  S49 = Reed switch [package=THT]  # not connected
  S50 = Reed switch [package=THT]  # not connected
  S51 = Reed switch [package=THT]  # not connected
  S52 = Reed switch [package=THT]  # not connected
  S53 = Reed switch [package=THT]  # not connected
  S54 = Reed switch [package=THT]  # not connected
  S55 = Reed switch [package=THT]  # not connected
  S56 = Reed switch [package=THT]  # not connected
  S57 = Reed switch [package=THT]  # not connected
  S58 = Reed switch [package=THT]  # not connected
  S59 = Reed switch [package=THT]  # not connected
  S60 = Reed switch [package=THT]  # not connected
  S61 = Reed switch [package=THT]  # not connected
  S62 = Reed switch [package=THT]  # not connected
  Raspberry_Pi1 = Raspberry Pi

nets:
  N1: S20.pin_1, S21.pin_1, S22.pin_1, S23.pin_1, S24.pin_1, S25.pin_1, S26.pin_1, S27.pin_1, S28.pin_1, Raspberry_Pi1.GND
  N2: S20.pin_2, S21.pin_2, S22.pin_2, S23.pin_2, S24.pin_2, S25.pin_2, S26.pin_2, S27.pin_2, S28.pin_2, Raspberry_Pi1.SPI_CE0_N
